// Logisim project Biblioteca de Portas.circ as structural Verilog: 8 circuits, main circuit Porta AND
module Porta_AND (
  input  in_1,
  input  in_2,
  output out_3
);

  wire transistor_2_out;

  Transistor #(.\type ("n")) transistor_1 (.in(transistor_2_out), .out(out_3), .gate(in_1));
  Transistor #(.\type ("n")) transistor_2 (.in(1'b1), .out(transistor_2_out), .gate(in_2));
  Pull_Resistor pull_resistor_1 (.node(out_3));

  // Notes on the sheet:
  //   out_3: pull=down
endmodule

module Porta_OR (
  input  in_1,
  input  in_2,
  output out_3
);

  Pull_Resistor pull_resistor_1 (.node(out_3));
  Transistor #(.\type ("n")) transistor_1 (.in(1'b1), .out(out_3), .gate(in_1));
  Transistor #(.\type ("n")) transistor_2 (.in(1'b1), .out(out_3), .gate(in_2));
endmodule

module Porta_NOT (
  input  in_1,
  output out_2
);

  Transistor transistor_1 (.in(1'b1), .out(out_2), .gate(in_1));
  Pull_Resistor pull_resistor_1 (.node(out_2));
endmodule

module Porta_NAND (
  input  in_1,
  input  in_2,
  output out_3
);

  wire porta_not_1_out_2, porta_not_2_out_2;

  Porta_NOT porta_not_1 (.out_2(porta_not_1_out_2), .in_1(in_1));
  Porta_NOT porta_not_2 (.out_2(porta_not_2_out_2), .in_1(in_2));
  Porta_OR porta_or_1 (.in_1(porta_not_1_out_2), .in_2(porta_not_2_out_2), .out_3(out_3));
endmodule

module Porta_NOR (
  input  in_1,
  input  in_2,
  output out_3
);

  wire porta_not_1_out_2, porta_not_2_out_2;

  Porta_NOT porta_not_1 (.out_2(porta_not_1_out_2), .in_1(in_1));
  Porta_NOT porta_not_2 (.out_2(porta_not_2_out_2), .in_1(in_2));
  Porta_AND porta_and_1 (.in_1(porta_not_1_out_2), .in_2(porta_not_2_out_2), .out_3(out_3));
endmodule

module Porta_XOR (
  input  in_1,
  input  in_2,
  output out_3
);

  wire porta_and_1_out_3, porta_and_2_out_3, porta_not_1_out_2, porta_not_2_out_2;

  Porta_NOT porta_not_1 (.out_2(porta_not_1_out_2), .in_1(in_2));
  Porta_NOT porta_not_2 (.out_2(porta_not_2_out_2), .in_1(in_1));
  Porta_AND porta_and_1 (.in_1(in_1), .in_2(porta_not_1_out_2), .out_3(porta_and_1_out_3));
  Porta_OR porta_or_1 (.in_1(porta_and_1_out_3), .in_2(porta_and_2_out_3), .out_3(out_3));
  Porta_AND porta_and_2 (.in_1(porta_not_2_out_2), .in_2(in_2), .out_3(porta_and_2_out_3));
endmodule

module Porta_XNOR (
  input  in_1,
  input  in_2,
  output out_3
);

  wire porta_and_1_out_3, porta_and_2_out_3, porta_not_1_out_2, porta_not_2_out_2;

  Porta_NOT porta_not_1 (.out_2(porta_not_1_out_2), .in_1(in_1));
  Porta_NOT porta_not_2 (.out_2(porta_not_2_out_2), .in_1(in_2));
  Porta_AND porta_and_1 (.in_1(porta_not_1_out_2), .in_2(porta_not_2_out_2), .out_3(porta_and_1_out_3));
  Porta_OR porta_or_1 (.in_1(porta_and_1_out_3), .in_2(porta_and_2_out_3), .out_3(out_3));
  Porta_AND porta_and_2 (.in_1(in_1), .in_2(in_2), .out_3(porta_and_2_out_3));
endmodule

module Mesa_de_Trabalho_Testes (
  input  in_1,
  input  in_2,
  input  in_3,
  input  in_4,
  input  in_5,
  input  in_6,
  input  in_7,
  input  in_8,
  input  in_9,
  input  in_10,
  input  in_11,
  input  in_12,
  input  in_13,
  output out_14,
  output out_15,
  output out_16,
  output out_17,
  output out_18,
  output out_19,
  output out_20,
  output out_21,
  output out_22,
  output out_23,
  output out_24,
  output out_25,
  output out_26
);

  Porta_NOT porta_not_1 (.out_2(out_18), .in_1(in_5));
  Porta_AND porta_and_1 (.in_1(in_1), .in_2(in_2), .out_3(out_14));
  and and_1 (out_15, in_1, in_2);
  Porta_OR porta_or_1 (.in_1(in_3), .in_2(in_4), .out_3(out_16));
  or or_1 (out_17, in_3, in_4);
  Porta_NAND porta_nand_1 (.in_1(in_6), .in_2(in_7), .out_3(out_19));
  nand nand_1 (out_20, in_6, in_7);
  Porta_NOR porta_nor_1 (.in_1(in_8), .in_2(in_9), .out_3(out_21));
  nor nor_1 (out_22, in_8, in_9);
  Porta_XOR porta_xor_1 (.out_3(out_23), .in_1(in_10), .in_2(in_11));
  xor xor_1 (out_24, in_10, in_11);
  Porta_XNOR porta_xnor_1 (.out_3(out_25), .in_1(in_12), .in_2(in_13));
  xnor xnor_1 (out_26, in_12, in_13);
endmodule
