// Logisim project Somador ajustável.circ as structural Verilog: 4 circuits, main circuit Somador Limitado
module Somador_Limitado (
  input  in_1
);

  wire comparador_de_igualdade_1_out_3;
  wire [3:0] d_ff_4_q, \somador_nº_de_4_bits_1_out_3 ;

  D_Flip_Flop d_ff_1 (
    .clk(in_1), .D(\somador_nº_de_4_bits_1_out_3 [3]), .Q(d_ff_4_q[3]),
    .reset(comparador_de_igualdade_1_out_3));  // open: Qn, preset, en
  D_Flip_Flop d_ff_2 (
    .clk(in_1), .D(\somador_nº_de_4_bits_1_out_3 [2]), .Q(d_ff_4_q[2]),
    .reset(comparador_de_igualdade_1_out_3));  // open: Qn, preset, en
  Hex_Digit_Display hex_digit_display_1 (.value(d_ff_4_q));  // open: dp
  D_Flip_Flop d_ff_3 (
    .clk(in_1), .D(\somador_nº_de_4_bits_1_out_3 [1]), .Q(d_ff_4_q[1]),
    .reset(comparador_de_igualdade_1_out_3));  // open: Qn, preset, en
  \Somador__Nº_de_4_bits  \somador_nº_de_4_bits_1  (
    .in_1(d_ff_4_q), .in_2(4'b0001), .out_3(\somador_nº_de_4_bits_1_out_3 ));
  D_Flip_Flop d_ff_4 (
    .clk(in_1), .D(\somador_nº_de_4_bits_1_out_3 [0]), .Q(d_ff_4_q[0]),
    .reset(comparador_de_igualdade_1_out_3));  // open: Qn, preset, en
  Comparador_de_Igualdade comparador_de_igualdade_1 (
    .in_1(4'b1001), .in_2(d_ff_4_q), .out_3(comparador_de_igualdade_1_out_3));
  Hex_Digit_Display hex_digit_display_2 (.value(\somador_nº_de_4_bits_1_out_3 ));  // open: dp
endmodule

module Soma_3_Bits (
  input  \Número_1 ,
  input  \Número_2 ,
  input  Carry_In,
  output Soma,
  output Carry_Out
);

  wire porta_and_1_out_3, porta_and_2_out_3, porta_xor_1_out_3;

  Porta_XOR porta_xor_1 (.out_3(porta_xor_1_out_3), .in_1(\Número_1 ), .in_2(\Número_2 ));
  Porta_AND porta_and_1 (.in_1(\Número_1 ), .in_2(\Número_2 ), .out_3(porta_and_1_out_3));
  Porta_AND porta_and_2 (.in_1(porta_xor_1_out_3), .in_2(Carry_In), .out_3(porta_and_2_out_3));
  Porta_XOR porta_xor_2 (.out_3(Soma), .in_1(porta_xor_1_out_3), .in_2(Carry_In));
  Porta_OR porta_or_1 (.in_1(porta_and_1_out_3), .in_2(porta_and_2_out_3), .out_3(Carry_Out));
endmodule

module \Somador__Nº_de_4_bits  (
  input  [3:0] in_1,
  input  [3:0] in_2,
  output [3:0] out_3
);

  wire soma_3_bits_1_carry_out, soma_3_bits_2_carry_out, soma_3_bits_3_carry_out;

  Soma_3_Bits soma_3_bits_1 (
    .\Número_1 (in_1[0]), .\Número_2 (in_2[0]), .Carry_In(1'b0), .Soma(out_3[0]),
    .Carry_Out(soma_3_bits_1_carry_out));
  Soma_3_Bits soma_3_bits_2 (
    .\Número_1 (in_1[1]), .\Número_2 (in_2[1]), .Carry_In(soma_3_bits_1_carry_out), .Soma(out_3[1]),
    .Carry_Out(soma_3_bits_2_carry_out));
  Soma_3_Bits soma_3_bits_3 (
    .\Número_1 (in_1[2]), .\Número_2 (in_2[2]), .Carry_In(soma_3_bits_2_carry_out), .Soma(out_3[2]),
    .Carry_Out(soma_3_bits_3_carry_out));
  Soma_3_Bits soma_3_bits_4 (
    .\Número_1 (in_1[3]), .\Número_2 (in_2[3]), .Carry_In(soma_3_bits_3_carry_out), .Soma(out_3[3]));  // open: Carry_Out
endmodule

module Comparador_de_Igualdade (
  input  [3:0] in_1,
  input  [3:0] in_2,
  output out_3
);

  wire porta_and_1_out_3, porta_and_2_out_3, porta_xnor_1_out_3, porta_xnor_2_out_3, porta_xnor_3_out_3,
       porta_xnor_4_out_3;

  Porta_XNOR porta_xnor_1 (.out_3(porta_xnor_1_out_3), .in_1(in_1[0]), .in_2(in_2[0]));
  Porta_XNOR porta_xnor_2 (.out_3(porta_xnor_2_out_3), .in_1(in_1[1]), .in_2(in_2[1]));
  Porta_XNOR porta_xnor_3 (.out_3(porta_xnor_3_out_3), .in_1(in_1[2]), .in_2(in_2[2]));
  Porta_XNOR porta_xnor_4 (.out_3(porta_xnor_4_out_3), .in_1(in_1[3]), .in_2(in_2[3]));
  Porta_AND porta_and_1 (.in_1(porta_xnor_1_out_3), .in_2(porta_xnor_2_out_3), .out_3(porta_and_1_out_3));
  Porta_AND porta_and_2 (.in_1(porta_xnor_3_out_3), .in_2(porta_xnor_4_out_3), .out_3(porta_and_2_out_3));
  Porta_AND porta_and_3 (.in_1(porta_and_1_out_3), .in_2(porta_and_2_out_3), .out_3(out_3));
endmodule
